# Fritzing sketch fritzing_gösterimi (saved by Fritzing 0.9.5d)
breadboards: 2

parts:
  T3_Vakfı2 = Generic shrouded header - 32 pins [package=THT]
  KEYPAD2 = Membrane Matrix Keypad
  DENEYAP_KART2 = DENEYAP OLED EKRAN [package="DIP (Dual Inline) [THT]"]  # not connected
  R1 = Resistor [tolerance=±5% resistance=220 package=THT]
  LED1 = LED - 5mm [color="Green (565nm)" package="5 mm [THT]"]
  LED2 = LED - 5mm [color="Red (633nm)" package="5 mm [THT]"]
  R2 = Resistor [tolerance=±5% resistance=220 package=THT]
  T3_Vakfı3 = Generic shrouded header - 32 pins [package=THT]
  KEYPAD3 = Membrane Matrix Keypad
  DENEYAP_KART3 = DENEYAP OLED EKRAN [package="DIP (Dual Inline) [THT]"]  # not connected
  R3 = Resistor [tolerance=±5% resistance=220 package=THT]
  R4 = Resistor [tolerance=±5% resistance=220 package=THT]
  LED3 = LED - 5mm [color="Green (565nm)" package="5 mm [THT]"]
  LED4 = LED - 5mm [color="Red (633nm)" package="5 mm [THT]"]

nets:
  N1: T3_Vakfı2.pin10, LED1.anode
  N2: T3_Vakfı2.pin11, LED2.anode
  N3: T3_Vakfı2.pin12, KEYPAD2.7
  N4: T3_Vakfı2.pin13, KEYPAD2.6
  N5: T3_Vakfı2.pin22, KEYPAD2.5
  N6: T3_Vakfı2.pin23, KEYPAD2.4
  N7: T3_Vakfı2.pin27, KEYPAD2.3
  N8: T3_Vakfı2.pin30, KEYPAD2.2
  N9: T3_Vakfı2.pin31, KEYPAD2.1
  N10: R1.Pin_0, R2.Pin_0
  N11: R1.Pin_1, LED1.cathode
  N12: LED2.cathode, R2.Pin_1
  N13: T3_Vakfı3.pin10, LED3.anode
  N14: T3_Vakfı3.pin11, LED4.anode
  N15: T3_Vakfı3.pin12, KEYPAD3.7
  N16: T3_Vakfı3.pin13, KEYPAD3.6
  N17: T3_Vakfı3.pin22, KEYPAD3.5
  N18: T3_Vakfı3.pin23, KEYPAD3.4
  N19: T3_Vakfı3.pin27, KEYPAD3.3
  N20: T3_Vakfı3.pin30, KEYPAD3.2
  N21: T3_Vakfı3.pin31, KEYPAD3.1
  N22: R3.Pin_0, R4.Pin_0
  N23: R3.Pin_1, LED3.cathode
  N24: R4.Pin_1, LED4.cathode

notes:
  DENEYAPKART-1
  DENEYAPKART-2

custom parts:
  Generic shrouded header - 32 pins: Ülkemizin mühendislik kaynakları kullanılarak geliştirilen Deneyap Kart; güçlü işlemcisi, dayanıklı tasarımı ve çok yönlü giriş/çıkış pinleri ile kullanıcılara Elektronik Programlama, Nesnelerin İnterneti (IoT) ve Yapay Zeka alanlarında başlangıç seviyesinden endüstriyel uygulamalara kadar her seviyede projeyi yapma imkanı sunuyor.
  Membrane Matrix Keypad: Membrane Matrix 3x4 Keypad
  DENEYAP OLED EKRAN: https://deneyapkart.org/
